# Fritzing sketch lolo-musicbox (saved by Fritzing 0.9.3b)

parts:
  Raspi = Raspberry Pi B+
  MFRC522_NFC_Reader = RFID-RC522-v3
  MCP3008_ADC = MCP3008 [package=dil16]
  RGB_LED = RGB LED (com. cathode, rgb) [package="5 mm [THT]"]
  R1 = Rotary Potentiometer (Large) [maximum_resistance=100kΩ package=THT]
  Power_Button = Round Pushbutton
  Next_Button = Round Pushbutton
  Play/Pause_Button = Round Pushbutton
  Prev_Button = Round Pushbutton
  R2 = Resistor [tolerance=±5% resistance=220 package="2512 [SMD]"]
  R3 = Resistor [tolerance=±5% resistance=220 package="2512 [SMD]"]
  R4 = Resistor [tolerance=±5% resistance=220 package="2512 [SMD]"]

nets:
  N1: Raspi.GPIO4, Power_Button.leg1
  N2: Raspi.GPIO17, Prev_Button.leg1
  N3: Raspi.GPIO27, Play/Pause_Button.leg1
  N4: Raspi.GPIO22, Next_Button.leg1
  3V3: Raspi.3V3, MFRC522_NFC_Reader.3.3V, MCP3008_ADC.VREF, MCP3008_ADC.VDD, R1.leg2
  N5: Raspi.GPIO10, MFRC522_NFC_Reader.MOSI
  N6: Raspi.GPIO9, MFRC522_NFC_Reader.MISO
  N7: Raspi.GPIO11, MFRC522_NFC_Reader.SCK
  N8: Raspi.GPIO5, MCP3008_ADC.CLK
  N9: Raspi.GPIO6, MCP3008_ADC.Dout
  N10: Raspi.GPIO13, MCP3008_ADC.Din
  N11: Raspi.GPIO19, MCP3008_ADC.CS/SHDN
  GND: Raspi.GND, MFRC522_NFC_Reader.GND, MCP3008_ADC.DGND, MCP3008_ADC.AGND, RGB_LED.common_cathode, R1.leg1, Power_Button.leg0, Next_Button.leg0, Play/Pause_Button.leg0, Prev_Button.leg0
  N12: Raspi.GPIO20, R2.Pin_0
  N13: Raspi.GPIO16, R3.Pin_0
  N14: Raspi.GPIO12, R4.Pin_0
  N15: Raspi.GPIO8, MFRC522_NFC_Reader.SDA
  N16: Raspi.GPIO25, MFRC522_NFC_Reader.RST
  N17: Raspi.GPIO24, MFRC522_NFC_Reader.IRQ
  N18: MCP3008_ADC.CH7, R1.wiper
  N19: RGB_LED.red_anode, R4.Pin_1
  N20: RGB_LED.green_anode, R3.Pin_1
  N21: RGB_LED.blue_anode, R2.Pin_1

custom parts:
  RFID-RC522-v3: A simple China made RFID-RC522 Reader (6x4 cm); do check the pin labels, as this is a MFRC522 based clone.
